// Logisim project alu.circ as structural Verilog: 2 circuits, main circuit alu
module alu (
  input  [31:0] A,
  input  [31:0] B,
  input  [3:0] ALUSel,
  output [31:0] Result
);

  wire less;
  wire [31:0] add, \and , divu, mul, mulh, mulhu, \or , remu, sll, slt, sra, srl, sub, \xor ;

  Shifter #(.width(32)) shifter_1 (.in(A), .\dist (B[4:0]), .out(sll));
  Shifter #(.width(32), .shift("lr")) shifter_2 (.in(A), .\dist (B[4:0]), .out(srl));
  Adder #(.width(32)) adder_1 (.a(A), .b(B), .out(add));  // open: cin, cout
  assign \and  = A & B;  // AND_Gate and_1, 32 bits wide
  assign \or  = A | B;  // OR_Gate or_1, 32 bits wide
  assign \xor  = A ^ B;  // XOR_Gate xor_1, 32 bits wide
  Comparator #(.width(32)) comparator_1 (.a(A), .b(B), .lt(less));  // open: gt, eq
  Multiplier #(.width(32)) multiplier_1 (.a(A), .b(B), .out(mul), .cout(mulhu));  // open: cin
  Divider #(.width(32)) divider_1 (.a(A), .b(B), .out(divu), .rem(remu));  // open: upper
  Shifter #(.width(32), .shift("ar")) shifter_3 (.in(A), .\dist (B[4:0]), .out(sra));
  Subtractor #(.width(32)) subtractor_1 (.a(A), .b(B), .out(sub));  // open: bin, bout
  Multiplexer #(.width(32), .enable("false")) multiplexer_1 (.in0({32{1'b0}}), .in1(32'h1), .out(slt), .sel(less));
  Multiplexer #(.select(4), .width(32), .enable("false")) multiplexer_2 (
    .in0(add), .in1(\and ), .in2(\or ), .in3(\xor ), .in4(srl), .in5(sra), .in6(sll), .in7(slt), .in8(divu),
    .in9(remu), .in10(mul), .in11(mulhu), .in12(sub), .in13(B), .in14(mulh), .out(Result), .sel(ALUSel));  // open: in15
  mulhEC mulhec_1 (.A(A), .B(B), .mulhu(mulhu), .mulh(mulh));

  // Notes on the sheet:
  //   INPUTS to your circuit
  //   DON'T CHANGE THE LOCATIONS OF THE INPUTS AND OUTPUTS!
  //   OUTPUT from your circuit
endmodule

module mulhEC (
  input  [31:0] A,
  input  [31:0] B,
  input  [31:0] mulhu,
  output [31:0] mulh
);

  wire and_1_out, and_2_out, and_3_out, and_4_out, comparator_1_lt, comparator_2_lt, comparator_3_gt,
       comparator_4_gt, comparator_5_gt, comparator_6_lt, comparator_7_lt, comparator_8_gt;
  wire [31:0] adder_1_out, adder_2_out, bit_extender_1_out, bit_extender_2_out, bit_extender_3_out,
       bit_extender_4_out, multiplier_1_out, multiplier_2_out, multiplier_3_out, multiplier_4_out,
       multiplier_5_cout, multiplier_6_out, multiplier_7_out, multiplier_8_out, multiplier_9_out;

  Comparator #(.width(32)) comparator_1 (.a(A), .b({32{1'b0}}), .lt(comparator_1_lt));  // open: gt, eq
  Comparator #(.width(32)) comparator_2 (.a(B), .b({32{1'b0}}), .lt(comparator_2_lt));  // open: gt, eq
  Comparator #(.width(32)) comparator_3 (.a(A), .b({32{1'b0}}), .gt(comparator_3_gt));  // open: eq, lt
  Comparator #(.width(32)) comparator_4 (.a(B), .b({32{1'b0}}), .gt(comparator_4_gt));  // open: eq, lt
  Comparator #(.width(32)) comparator_5 (.a(A), .b({32{1'b0}}), .gt(comparator_5_gt));  // open: eq, lt
  Comparator #(.width(32)) comparator_6 (.a(B), .b({32{1'b0}}), .lt(comparator_6_lt));  // open: gt, eq
  Multiplier #(.width(32)) multiplier_1 (.a({32{1'b1}}), .b(A), .out(multiplier_1_out));  // open: cin, cout
  Comparator #(.width(32)) comparator_7 (.a(A), .b({32{1'b0}}), .lt(comparator_7_lt));  // open: gt, eq
  Comparator #(.width(32)) comparator_8 (.a(B), .b({32{1'b0}}), .gt(comparator_8_gt));  // open: eq, lt
  and and_1 (and_1_out, comparator_3_gt, comparator_4_gt);
  and and_2 (and_2_out, comparator_5_gt, comparator_6_lt);
  Adder #(.width(32)) adder_1 (.a(multiplier_1_out), .b(mulhu), .out(adder_1_out));  // open: cin, cout
  Multiplier #(.width(32)) multiplier_2 (.a({32{1'b1}}), .b(B), .out(multiplier_2_out));  // open: cin, cout
  and and_3 (and_3_out, comparator_1_lt, comparator_2_lt);
  Multiplier #(.width(32)) multiplier_3 (.a(A), .b({32{1'b1}}), .out(multiplier_3_out));  // open: cin, cout
  Multiplier #(.width(32)) multiplier_4 (.a(B), .b({32{1'b1}}), .out(multiplier_4_out));  // open: cin, cout
  assign bit_extender_1_out = {{31{1'b0}}, and_2_out};  // Bit_Extender bit_extender_1
  and and_4 (and_4_out, comparator_7_lt, comparator_8_gt);
  Adder #(.width(32)) adder_2 (.a(multiplier_2_out), .b(mulhu), .out(adder_2_out));  // open: cin, cout
  assign bit_extender_2_out = {{31{1'b0}}, and_3_out};  // Bit_Extender bit_extender_2
  Multiplier #(.width(32)) multiplier_5 (
    .a(multiplier_3_out), .b(multiplier_4_out), .cout(multiplier_5_cout));  // open: out, cin
  assign bit_extender_3_out = {{31{1'b0}}, and_4_out};  // Bit_Extender bit_extender_3
  assign bit_extender_4_out = {{31{1'b0}}, and_1_out};  // Bit_Extender bit_extender_4
  Multiplier #(.width(32)) multiplier_6 (
    .a(bit_extender_1_out), .b(adder_1_out), .out(multiplier_6_out));  // open: cin, cout
  Multiplier #(.width(32)) multiplier_7 (
    .a(bit_extender_3_out), .b(adder_2_out), .out(multiplier_7_out));  // open: cin, cout
  Multiplier #(.width(32)) multiplier_8 (
    .a(bit_extender_2_out), .b(multiplier_5_cout), .out(multiplier_8_out));  // open: cin, cout
  Multiplier #(.width(32)) multiplier_9 (.a(bit_extender_4_out), .b(mulhu), .out(multiplier_9_out));  // open: cin, cout
  assign mulh = multiplier_8_out | multiplier_9_out | multiplier_6_out | multiplier_7_out;  // OR_Gate or_1, 32 bits wide
endmodule
